// Logisim project HajarNaghiyeva.circ as structural Verilog: 4 circuits, main circuit main
// c
module main (
);

  wire _0, _1, _2, _3, _4, _5, _6, _7, _8, _9, bcd_adder_2_out_5, bcd_adder_3_out_5, bcd_adder_4_out_5, C1,
       C2, D1, D2, nor_1_out, not_1_out, OR1, or_1_out, or_2_out, priority_encoder_1_gs, tunnel, tunnel_t,
       tunnel_t_t;
  wire [0:0] BA0;
  wire [3:0] BA1, BA2, BA3, BA4, BS0, BS1, BS2, BS3, controlled_buffer_1_out, M1, M2, M3, M4, M5,
       priority_encoder_1_out, S10, S11, S12, S13, S14, S21, S22, S23, S24;

  Button u__2 (.out(_2));
  Button u__1 (.out(_1));
  Button u__4 (.out(_4));
  Button u__5 (.out(_5));
  Button u__8 (.out(_8));
  Button u__7 (.out(_7));
  Button u__0 (.out(_0));
  Button u__3 (.out(_3));
  Button u__6 (.out(_6));
  Button u__9 (.out(_9));
  Priority_Encoder #(.select(4)) priority_encoder_1 (
    .in0(_0), .in1(_1), .in2(_2), .in3(_3), .in4(_4), .in5(_5), .in6(_6), .in7(_7), .in8(_8), .in9(_9),
    .out(priority_encoder_1_out), .gs(priority_encoder_1_gs));  // open: in10, in11, in12, in13, in14, in15, en_out, en_in
  Button C (.out(C1));
  Button button (.out(tunnel));
  Button button_2 (.out(tunnel_t));
  Button button_3 (.out(tunnel_t_t));
  nor nor_1 (nor_1_out, OR1, D1);
  D_Flip_Flop d_ff_1 (.clk(tunnel_t_t), .D(nor_1_out), .Qn(D2), .reset(C1));  // open: Q, preset, en
  not not_1 (not_1_out, tunnel_t_t);
  or or_1 (or_1_out, priority_encoder_1_gs, tunnel_t_t);
  Shift_Register #(.width(4), .length(5)) shift_register_1 (
    .shift(not_1_out), .in(priority_encoder_1_out), .clk(or_1_out), .load(tunnel_t_t), .clr(C2), .d0(M5),
    .q0(S14), .d1(M4), .q1(S13), .d2(M3), .q2(S12), .d3(M2), .q3(S11), .d4(M1), .q4(S10));  // open: out
  Shift_Register #(.width(4), .length(4)) shift_register_2 (
    .shift(1'b0), .clk(or_2_out), .load(or_2_out), .d0(S14), .q0(S24), .d1(S13), .q1(S23), .d2(S12),
    .q2(S22), .d3(S11), .q3(S21));  // open: in, out, clr
  or or_2 (or_2_out, tunnel, tunnel_t);
  Hex_Digit_Display hex_digit_display_1 (.value(S11));  // open: dp
  Hex_Digit_Display hex_digit_display_2 (.value(controlled_buffer_1_out));  // open: dp
  assign controlled_buffer_1_out = D2 ? S10 : 4'bz;  // Controlled_Buffer controlled_buffer_1
  or or_3 (C2, C1, or_2_out);
  D_Flip_Flop d_ff_2 (.clk(tunnel), .D(tunnel), .Q(D1), .reset(C1));  // open: Qn, preset, en
  Hex_Digit_Display hex_digit_display_3 (.value(S13));  // open: dp
  Hex_Digit_Display hex_digit_display_4 (.value(S12));  // open: dp
  Hex_Digit_Display hex_digit_display_5 (.value(S14));  // open: dp
  bcd_adder bcd_adder_1 (.in_3(S11), .in_2(S21), .in_1(bcd_adder_2_out_5), .out_4(BA1), .out_5(BA0[0]));
  Multiplexer #(.width(4)) multiplexer_1 (.in0(4'b0000), .in1({3'b000, BA0[0]}), .out(M1), .sel(D1));  // open: en
  bcd_adder bcd_adder_2 (.in_3(S12), .in_2(S22), .in_1(bcd_adder_3_out_5), .out_4(BA2), .out_5(bcd_adder_2_out_5));
  subtractor subtractor_1 (
    .in_1(S11), .in_2(S12), .in_3(S13), .in_4(S14), .in_5(S21), .out_10(BS0), .out_11(BS1), .out_12(BS2),
    .out_13(BS3), .in_8(S24), .in_7(S23), .in_6(S22), .out_9(OR1));
  Multiplexer #(.width(4)) multiplexer_2 (.in0(BS0), .in1(BA1), .out(M2), .sel(D1));  // open: en
  bcd_adder bcd_adder_3 (.in_3(S13), .in_2(S23), .in_1(bcd_adder_4_out_5), .out_4(BA3), .out_5(bcd_adder_3_out_5));
  Multiplexer #(.width(4)) multiplexer_3 (.in0(BS1), .in1(BA2), .out(M3), .sel(D1));  // open: en
  bcd_adder bcd_adder_4 (.in_3(S14), .in_2(S24), .in_1(1'b0), .out_4(BA4), .out_5(bcd_adder_4_out_5));
  Multiplexer #(.width(4)) multiplexer_4 (.in0(BS2), .in1(BA3), .out(M4), .sel(D1));  // open: en
  Multiplexer #(.width(4)) multiplexer_5 (.in0(BS3), .in1(BA4), .out(M5), .sel(D1));  // open: en

  // Notes on the sheet:
  //   CALCULATOR
  //   BCD ADDER
  //   BCD SUBTRACTOR
endmodule

module bcd_adder (
  input  in_1,
  input  [3:0] in_2,
  input  [3:0] in_3,
  output [3:0] out_4,
  output out_5
);

  wire adder_1_cout, and_1_out, and_2_out;
  wire [3:0] adder_1_out;

  Adder #(.width(4)) adder_1 (.a(in_2), .b(in_3), .out(adder_1_out), .cin(in_1), .cout(adder_1_cout));
  and and_1 (and_1_out, adder_1_out[3], adder_1_out[2]);
  or or_1 (out_5, adder_1_cout, and_1_out, and_2_out);
  and and_2 (and_2_out, adder_1_out[3], adder_1_out[1]);
  Adder #(.width(4)) adder_2 (.a(adder_1_out), .b({1'b0, {2{out_5}}, 1'b0}), .out(out_4));  // open: cin, cout
endmodule

module subtractor (
  input  [3:0] in_1,
  input  [3:0] in_2,
  input  [3:0] in_3,
  input  [3:0] in_4,
  input  [3:0] in_5,
  input  [3:0] in_6,
  input  [3:0] in_7,
  input  [3:0] in_8,
  output out_9,
  output [3:0] out_10,
  output [3:0] out_11,
  output [3:0] out_12,
  output [3:0] out_13
);

  wire bcd_adder_2_out_5, bcd_adder_3_out_5, bcd_adder_4_out_5, bcd_adder_6_out_5, bcd_adder_7_out_5,
       bcd_adder_8_out_5;
  wire [3:0] _011, _012, _013, _014, _021, _022, _023, _024, n9_th_comp_1_out_2, n9_th_comp_2_out_2,
       n9_th_comp_3_out_2, n9_th_comp_4_out_2, n9_th_comp_5_out_2, n9_th_comp_6_out_2, n9_th_comp_7_out_2,
       n9_th_comp_8_out_2;

  _9_th_comp u_9_th_comp_1 (.in_1(in_1), .out_2(n9_th_comp_1_out_2));
  bcd_adder bcd_adder_1 (.in_3(n9_th_comp_1_out_2), .in_2(in_5), .in_1(bcd_adder_2_out_5), .out_4(_011), .out_5(out_9));
  Multiplexer #(.width(4)) multiplexer_1 (.in0(_021), .in1(_011), .out(out_10), .sel(out_9));  // open: en
  _9_th_comp u_9_th_comp_2 (.in_1(in_2), .out_2(n9_th_comp_2_out_2));
  bcd_adder bcd_adder_2 (
    .in_3(n9_th_comp_2_out_2), .in_2(in_6), .in_1(bcd_adder_3_out_5), .out_4(_012), .out_5(bcd_adder_2_out_5));
  Multiplexer #(.width(4)) multiplexer_2 (.in0(_022), .in1(_012), .out(out_11), .sel(out_9));  // open: en
  _9_th_comp u_9_th_comp_3 (.in_1(in_3), .out_2(n9_th_comp_3_out_2));
  bcd_adder bcd_adder_3 (
    .in_3(n9_th_comp_3_out_2), .in_2(in_7), .in_1(bcd_adder_4_out_5), .out_4(_013), .out_5(bcd_adder_3_out_5));
  Multiplexer #(.width(4)) multiplexer_3 (.in0(_023), .in1(_013), .out(out_12), .sel(out_9));  // open: en
  Multiplexer #(.width(4)) multiplexer_4 (.in0(_024), .in1(_014), .out(out_13), .sel(out_9));  // open: en
  _9_th_comp u_9_th_comp_4 (.in_1(in_4), .out_2(n9_th_comp_4_out_2));
  bcd_adder bcd_adder_4 (.in_3(n9_th_comp_4_out_2), .in_2(in_8), .in_1(1'b1), .out_4(_014), .out_5(bcd_adder_4_out_5));
  _9_th_comp u_9_th_comp_5 (.in_1(_011), .out_2(n9_th_comp_5_out_2));
  bcd_adder bcd_adder_5 (
    .in_3(4'b0000), .in_2(n9_th_comp_5_out_2), .in_1(bcd_adder_6_out_5), .out_4(_021));  // open: out_5
  _9_th_comp u_9_th_comp_6 (.in_1(_012), .out_2(n9_th_comp_6_out_2));
  bcd_adder bcd_adder_6 (
    .in_3(4'b0000), .in_2(n9_th_comp_6_out_2), .in_1(bcd_adder_7_out_5), .out_4(_022),
    .out_5(bcd_adder_6_out_5));
  _9_th_comp u_9_th_comp_7 (.in_1(_013), .out_2(n9_th_comp_7_out_2));
  bcd_adder bcd_adder_7 (
    .in_3(4'b0000), .in_2(n9_th_comp_7_out_2), .in_1(bcd_adder_8_out_5), .out_4(_023),
    .out_5(bcd_adder_7_out_5));
  _9_th_comp u_9_th_comp_8 (.in_1(_014), .out_2(n9_th_comp_8_out_2));
  bcd_adder bcd_adder_8 (
    .in_3(4'b0000), .in_2(n9_th_comp_8_out_2), .in_1(1'b1), .out_4(_024), .out_5(bcd_adder_8_out_5));
endmodule

module _9_th_comp (
  input  [3:0] in_1,
  output [3:0] out_2
);

  wire not_1_out, not_2_out, not_3_out;

  not not_1 (not_1_out, in_1[3]);
  not not_2 (not_2_out, in_1[2]);
  not not_3 (not_3_out, in_1[1]);
  not not_4 (out_2[0], in_1[0]);
  and and_1 (out_2[3], not_1_out, not_2_out, not_3_out);
  xor xor_1 (out_2[2], in_1[2], in_1[1]);

  assign out_2[1] = in_1[1];

  // Other names for the same wires on the sheet: I4 = in_1[0]; I2 = in_1[2]; I1 = in_1[3]; I3 = in_1[1]
endmodule
